// Logisim project sim.circ as structural Verilog: 7 circuits, main circuit main
module main (
);

  wire and_1_out, clock_1_out, control_1_alu_up, control_1_busmult_s0, control_1_busmult_s1,
       control_1_io_out, control_1_io_s0, control_1_mar_up, control_1_nalu_co, control_1_nalu_lo,
       control_1_nbusmult_oe, control_1_nlar_lo, control_1_nmar_co, control_1_npc_co, control_1_npc_lo,
       control_1_nram_oe, control_1_pc_up, control_1_ram_we, control_1_rammult_s0, not_1_out, not_2_out,
       not_3_out, process_1_databus_zc, process_1_mar_zc, RST_out, s_r_ff_1_q, s_r_ff_2_q;
  wire [6:0] keyboard_1_data;
  wire [11:0] bit_extender_1_out, process_1_out, process_1_pc_out, register_1_out;

  Clock clock_1 (.out(clock_1_out));
  Button RST (.out(RST_out));
  not not_1 (not_1_out, process_1_mar_zc);
  not not_2 (not_2_out, RST_out);
  S_R_Flip_Flop #(.trigger("high")) s_r_ff_1 (
    .S(not_1_out), .clk(1'b1), .R(RST_out), .Q(s_r_ff_1_q));  // open: Qn, preset, reset, en
  and and_1 (and_1_out, s_r_ff_1_q, process_1_mar_zc);
  S_R_Flip_Flop #(.trigger("high")) s_r_ff_2 (
    .S(and_1_out), .clk(1'b1), .R(RST_out), .Q(s_r_ff_2_q));  // open: Qn, preset, reset, en
  control control_1 (
    .PC(process_1_pc_out), .CLK(clock_1_out), .FLAGS_RESET(RST_out), .FLAGS_RFS(RST_out),
    .FLAGS_RFR(s_r_ff_2_q), .FLAGS_BZI(process_1_databus_zc), .nLPC_RESET(not_2_out),
    .nPC_LO(control_1_npc_lo), .nPC_CO(control_1_npc_co), .PC_UP(control_1_pc_up),
    .nMAR_CO(control_1_nmar_co), .MAR_UP(control_1_mar_up), .nLAR_LO(control_1_nlar_lo),
    .RAMMULT_S0(control_1_rammult_s0), .RAM_WE(control_1_ram_we), .nRAM_OE(control_1_nram_oe),
    .BUSMULT_S0(control_1_busmult_s0), .BUSMULT_S1(control_1_busmult_s1),
    .nBUSMULT_OE(control_1_nbusmult_oe), .nALU_LO(control_1_nalu_lo), .nALU_CO(control_1_nalu_co),
    .ALU_UP(control_1_alu_up), .IO_S0(control_1_io_s0), .IO_OUT(control_1_io_out));
  Keyboard #(.trigger("falling")) keyboard_1 (
    .clk(register_1_out[7]), .re(1'b1), .clr(RST_out), .data(keyboard_1_data));  // open: avail
  assign bit_extender_1_out = {{5{1'b0}}, keyboard_1_data};  // Bit_Extender bit_extender_1
  process process_1 (
    .CLK(clock_1_out), .MAR_UP(control_1_mar_up), .nMAR_CO(control_1_nmar_co), .nMAR_RESET(not_2_out),
    .nLAR_LO(control_1_nlar_lo), .RAMMULT_S0(control_1_rammult_s0), .RAM_WE(control_1_ram_we),
    .nRAM_OE(control_1_nram_oe), .nPC_LO(control_1_npc_lo), .PC_UP(control_1_pc_up),
    .nPC_CO(control_1_npc_co), .nALU_LO(control_1_nalu_lo), .ALU_UP(control_1_alu_up),
    .nALU_CO(control_1_nalu_co), .nBUSMULT_OE(control_1_nbusmult_oe), .BUSMULT_S1(control_1_busmult_s1),
    .BUSMULT_S0(control_1_busmult_s0), .IO_S0(control_1_io_s0), .MAR_ZC(process_1_mar_zc),
    .DATABUS_ZC(process_1_databus_zc), .PC_OUT(process_1_pc_out), .OUT(process_1_out), .IN(bit_extender_1_out));
  TTY #(.trigger("falling")) tty_1 (.data(register_1_out[6:0]), .clk(register_1_out[7]), .clr(RST_out));  // open: we
  not not_3 (not_3_out, control_1_io_out);
  register register_1 (
    .nLO(not_3_out), .UP(1'b1), .nCO(1'b1), .CLK(clock_1_out), .nRESET(1'b1), .IN(process_1_out),
    .OUT(register_1_out));
endmodule

module register (
  input  nLO,
  input  UP,
  input  nCO,
  input  CLK,
  input  nRESET,
  input  [11:0] IN,
  output [11:0] OUT
);

  wire and_1_out, and_2_out, not_1_out, or_1_out;

  and and_1 (and_1_out, ~UP, ~nCO);  // AND_Gate
  or or_1 (or_1_out, ~nLO, and_1_out);  // OR_Gate
  and and_2 (and_2_out, nLO, ~nCO);  // AND_Gate
  not not_1 (not_1_out, nRESET);
  Counter #(.width(12), .max('hfff)) counter_1 (
    .load(or_1_out), .D(IN), .count(and_2_out), .Q(OUT), .clk(CLK), .clr(not_1_out));  // open: carry
endmodule

module process (
  input  CLK,
  input  MAR_UP,
  input  nMAR_CO,
  input  nMAR_RESET,
  input  nLAR_LO,
  input  RAMMULT_S0,
  input  RAM_WE,
  input  nRAM_OE,
  input  nPC_LO,
  input  PC_UP,
  input  nPC_CO,
  input  nALU_LO,
  input  ALU_UP,
  input  nALU_CO,
  input  nBUSMULT_OE,
  input  BUSMULT_S1,
  input  BUSMULT_S0,
  input  IO_S0,
  input  [11:0] IN,
  output MAR_ZC,
  output DATABUS_ZC,
  output [11:0] PC_OUT,
  output [11:0] OUT
);

  wire not_1_out, not_2_out;
  wire [11:0] ALU_out, LAR_out, MAR_out, multiplexer_1_out, multiplexer_2_out;
  wire [12:0] bit_extender_1_out;

  register MAR (.nLO(1'b1), .UP(MAR_UP), .nCO(nMAR_CO), .CLK(CLK), .nRESET(nMAR_RESET), .IN({12{1'b0}}), .OUT(MAR_out));
  register LAR (.nLO(nLAR_LO), .UP(1'b1), .nCO(1'b1), .CLK(CLK), .nRESET(1'b1), .IN(PC_OUT), .OUT(LAR_out));
  register PC (.nLO(nPC_LO), .UP(PC_UP), .nCO(nPC_CO), .CLK(CLK), .nRESET(1'b1), .IN(multiplexer_2_out), .OUT(PC_OUT));
  zc zc_1 (.IN(MAR_out), .OUT(MAR_ZC));
  Multiplexer #(.width(12)) multiplexer_1 (
    .in0(MAR_out), .in1(LAR_out), .out(multiplexer_1_out), .sel(RAMMULT_S0), .en(1'b1));
  Multiplexer #(.select(2), .width(12)) multiplexer_2 (
    .in0(PC_OUT), .in1(IN), .in2(ALU_out), .out(multiplexer_2_out), .sel({BUSMULT_S1, BUSMULT_S0}),
    .en(not_1_out));  // open: in3
  not not_1 (not_1_out, nBUSMULT_OE);
  assign bit_extender_1_out = {{1{RAMMULT_S0}}, multiplexer_1_out};  // Bit_Extender bit_extender_1
  not not_2 (not_2_out, nRAM_OE);
  RAM #(.addrWidth(13), .dataWidth(12), .bus("separate")) ram_1 (
    .addr(bit_extender_1_out), .din(multiplexer_2_out), .data(multiplexer_2_out), .str(RAM_WE), .sel(1'b1),
    .clk(CLK), .ld(not_2_out), .clr(1'b0));
  Pull_Resistor pull_resistor_1 (.node(multiplexer_2_out));
  register ALU (
    .nLO(nALU_LO), .UP(ALU_UP), .nCO(nALU_CO), .CLK(CLK), .nRESET(1'b1), .IN(multiplexer_2_out), .OUT(ALU_out));
  zc zc_2 (.IN(multiplexer_2_out), .OUT(DATABUS_ZC));
  Multiplexer #(.width(12)) multiplexer_3 (.in0(ALU_out), .in1(multiplexer_2_out), .out(OUT), .sel(IO_S0), .en(1'b1));
endmodule

module control (
  input  [11:0] PC,
  input  CLK,
  input  FLAGS_RESET,
  input  FLAGS_RFS,
  input  FLAGS_RFR,
  input  FLAGS_BZI,
  input  nLPC_RESET,
  output nPC_LO,
  output nPC_CO,
  output PC_UP,
  output nMAR_CO,
  output MAR_UP,
  output nLAR_LO,
  output RAMMULT_S0,
  output RAM_WE,
  output nRAM_OE,
  output BUSMULT_S0,
  output BUSMULT_S1,
  output nBUSMULT_OE,
  output nALU_LO,
  output nALU_CO,
  output ALU_UP,
  output IO_S0,
  output IO_OUT
);

  wire FLAGS_ACT, FLAGS_BZL, FLAGS_ELT, FLAGS_SLT, LPC_UP, nLPC_CO, not_1_out, not_2_out, nPHASE_CO,
       PHASE_RESET, reset_1_out_3;
  wire [2:0] rom_1_data;
  wire [10:5] flags_register_1_slf;
  wire [11:0] register_1_out, register_2_out;

  not not_1 (not_1_out, CLK);
  ROM #(.addrWidth(12), .dataWidth(3)) rom_1 (.addr(PC), .data(rom_1_data), .sel(1'b1));
  register register_1 (
    .nLO(1'b1), .UP(1'b1), .nCO(1'b0), .CLK(not_1_out), .nRESET(not_2_out), .IN({12{1'b0}}),
    .OUT(register_1_out));
  flags_register flags_register_1 (
    .CLK(CLK), .RESET(FLAGS_RESET), .RFS(FLAGS_RFS), .RFR(FLAGS_RFR), .BZI(FLAGS_BZI), .BZL(FLAGS_BZL),
    .SLT(FLAGS_SLT), .ELT(FLAGS_ELT), .ACT(FLAGS_ACT), .RF(flags_register_1_slf[9]),
    .BZF(flags_register_1_slf[8]), .SLF(flags_register_1_slf[5]), .ELF(flags_register_1_slf[6]),
    .ACF(flags_register_1_slf[7]));
  register register_2 (
    .nLO(1'b1), .UP(LPC_UP), .nCO(nLPC_CO), .CLK(CLK), .nRESET(nLPC_RESET), .IN({12{1'b0}}),
    .OUT(register_2_out));
  zc ZC (.IN(register_2_out), .OUT(flags_register_1_slf[10]));
  not not_2 (not_2_out, reset_1_out_3);
  reset reset_1 (.RESET(PHASE_RESET), .CLK(CLK), .out_3(reset_1_out_3));
  ROM #(.addrWidth(11), .dataWidth(25)) rom_2 (
    .addr({flags_register_1_slf, register_1_out[1:0], rom_1_data}),
    .data({IO_OUT, IO_S0, ALU_UP, nALU_CO, nALU_LO, nBUSMULT_OE, BUSMULT_S1, BUSMULT_S0, nRAM_OE, RAM_WE, RAMMULT_S0, LPC_UP, nLPC_CO, nLAR_LO, MAR_UP, nMAR_CO, PC_UP, nPC_CO, nPC_LO, PHASE_RESET, nPHASE_CO, FLAGS_BZL, FLAGS_ACT, FLAGS_ELT, FLAGS_SLT}),
    .sel(1'b1));

  // Notes on the sheet:
  //   Program ROM
  //   contents of rom_1 (hex, n*v repeats v):
  //   0 4 1 2 0 4 2 7 4 3 1 5 3 5 2 2 128*0 6 128*1 6 2 2 2 1 1 4 3 3 3 48*1 2 2 2 3 3 128*0 6 128*1 6 2
  //   128*0 6 128*1 6 3 3 3 128*0 6 128*1 6 2 2 2 5 0 4 3 3 3 42*1 4 1 2 2 0 3 3 5 2 2 2 0 0 5 0 4 3 3 3
  //   48*1 4 1 2 0 3 5 2 2 2 0 5 3 3 3 0 5
  //   µcode ROM
  //   contents of rom_2 (hex, n*v repeats v):
  //   281ad0 281ad0 391d70 391970 3812d8 3812d8 1b81b70 239b74 591b74 191b64 391ad0 391ad0 391b70 385ad8
  //   6*391ad0 385ab0 385ab0 10*391ad0 4*391a70 390a70 392a70 6*391a70 390a70 392a70 6*391a70 390a70
  //   392a70 6*391a70 390a70 392a70 391a70 391a70 4*391b70 392b70 390b70 6*391b70 392b70 390b70 6*391b70
  //   392b70 390b70 6*391b70 392b70 390b70 391b70 391b70 32*391af0 591b70 191b70 359ad0 359ad0 3512d8
  //   3512d8 1391b70 239b70 391ad0 391ad0 391d74 391974 391b70 385ad8 6*391ad0 385ab0 385ab0 10*391ad0
  //   4*391a70 390a70 392a70 6*391a70 390a70 392a70 6*391a70 390a70 392a70 6*391a70 390a70 392a70 391a70
  //   391a70 4*391b70 392b70 390b70 6*391b70 392b70 390b70 6*391b70 392b70 390b70 6*391b70 392b70 390b70
  //   391b70 391b70 32*391af0 281ad0 281ad0 391d70 391970 3812d8 3812d8 1b81b70 239b74 591b74 191b64
  //   391ad0 391ad0 385ad8 391b70 6*391ad0 391b72 391a71 10*391ad0 4*391a70 390a70 392a70 6*391a70 390a70
  //   392a70 6*391a70 390a70 392a70 6*391a70 390a70 392a70 391a70 391a70 4*391b70 392b70 390b70 6*391b70
  //   392b70 390b70 6*391b70 392b70 390b70 6*391b70 392b70 390b70 391b70 391b70 32*391af0 591b70 191b70
  //   359ad0 359ad0 3512d8 3512d8 1391b70 239b70 391ad0 391ad0 391d74 391974 385ad8 391b70 6*391ad0 391b72
  //   391a71 10*391ad0 4*391a70 390a70 392a70 6*391a70 390a70 392a70 6*391a70 390a70 392a70 6*391a70
  //   390a70 392a70 391a70 391a70 4*391b70 392b70 390b70 6*391b70 392b70 390b70 6*391b70 392b70 390b70
  //   6*391b70 392b70 390b70 391b70 391b70 32*391af0 8*3992d0 8*39dd70 16*391ad0 8*3992d0 8*39dd70
  //   16*391ad0 8*3992d0 8*39dd70 16*391ad0 8*3992d0 8*39dd70 16*391ad0 8*3992d0 8*39dd70 16*391ad0
  //   8*3992d0 8*39dd70 16*391ad0 8*3992d0 8*39dd70 16*391ad0 8*3992d0 8*39dd70 16*391ad0 8*3992d0
  //   8*39dd70 16*391ad0 8*3992d0 8*39dd70 16*391ad0 8*3992d0 8*39dd70 16*391ad0 8*3992d0 8*39dd70
  //   16*391ad0 8*3992d0 8*39dd70 16*391ad0 8*3992d0 8*39dd70 16*391ad0 8*3992d0 8*39dd70 16*391ad0
  //   8*3992d0 8*39dd70 16*391ad0 281ad0 281ad0 391d70 391970 3812d8 3812d8 1b81b70 239b74 591b74 191b64
  //   391ad0 391ad0 391b70 385ad8 6*391ad0 385ab0 385ab0 10*391ad0 4*391a70 31db71 392a70 6*391a70 31db71
  //   392a70 6*391a70 31db71 392a70 6*391a70 31db71 392a70 391a70 391a70 4*391b70 392b70 31db72 6*391b70
  //   392b70 31db72 6*391b70 392b70 31db72 6*391b70 392b70 31db72 391b70 391b70 32*391af0 591b70 191b70
  //   359ad0 359ad0 3512d8 3512d8 1391b70 239b70 391ad0 391ad0 391d74 391974 391b70 385ad8 6*391ad0 385ab0
  //   385ab0 10*391ad0 4*391a70 31db71 392a70 6*391a70 31db71 392a70 6*391a70 31db71 392a70 6*391a70
  //   31db71 392a70 391a70 391a70 4*391b70 392b70 31db72 6*391b70 392b70 31db72 6*391b70 392b70 31db72
  //   6*391b70 392b70 31db72 391b70 391b70 32*391af0 281ad0 281ad0 391d70 391970 3812d8 3812d8 1b81b70
  //   239b74 591b74 191b64 391ad0 391ad0 385ad8 391b70 6*391ad0 391b72 391a71 10*391ad0 4*391a70 31db71
  //   392a70 6*391a70 31db71 392a70 6*391a70 31db71 392a70 6*391a70 31db71 392a70 391a70 391a70 4*391b70
  //   392b70 31db72 6*391b70 392b70 31db72 6*391b70 392b70 31db72 6*391b70 392b70 31db72 391b70 391b70
  //   32*391af0 591b70 191b70 359ad0 359ad0 3512d8 3512d8 1391b70 239b70 391ad0 391ad0 391d74 391974
  //   385ad8 391b70 6*391ad0 391b72 391a71 10*391ad0 4*391a70 31db71 392a70 6*391a70 31db71 392a70
  //   6*391a70 31db71 392a70 6*391a70 31db71 392a70 391a70 391a70 4*391b70 392b70 31db72 6*391b70 392b70
  //   31db72 6*391b70 392b70 31db72 6*391b70 392b70 31db72 391b70 391b70 32*391af0 8*3992d0 8*39dd70
  //   16*391ad0 8*3992d0 8*39dd70 16*391ad0 8*3992d0 8*39dd70 16*391ad0 8*3992d0 8*39dd70 16*391ad0
  //   8*3992d0 8*39dd70 16*391ad0 8*3992d0 8*39dd70 16*391ad0 8*3992d0 8*39dd70 16*391ad0 8*3992d0
  //   8*39dd70 16*391ad0 8*3992d0 8*39dd70 16*391ad0 8*3992d0 8*39dd70 16*391ad0 8*3992d0 8*39dd70
  //   16*391ad0 8*3992d0 8*39dd70 16*391ad0 8*3992d0 8*39dd70 16*391ad0 8*3992d0 8*39dd70 16*391ad0
  //   8*3992d0 8*39dd70 16*391ad0 8*3992d0 8*39dd70 16*391ad0
endmodule

module zc (
  input  [11:0] IN,
  output OUT
);

  wire or_1_out;

  or or_1 (or_1_out, IN[0], IN[1], IN[2], IN[3], IN[4], IN[5], IN[6], IN[7], IN[8], IN[9], IN[10], IN[11]);
  not not_1 (OUT, or_1_out);
endmodule

module flags_register (
  input  CLK,
  input  RESET,
  input  RFS,
  input  RFR,
  input  BZI,
  input  BZL,
  input  SLT,
  input  ELT,
  input  ACT,
  output RF,
  output BZF,
  output SLF,
  output ELF,
  output ACF
);

  wire and_1_out, and_2_out, and_3_out, and_4_out, and_5_out, nor_1_out, nor_4_out, not_1_out, not_2_out,
       or_1_out, or_2_out;

  not not_1 (not_1_out, RFS);
  and and_1 (and_1_out, CLK, not_1_out, RFR);
  and and_2 (and_2_out, ~RESET, BZI);  // AND_Gate
  J_K_Flip_Flop j_k_ff_1 (.J(SLT), .clk(CLK), .K(SLT), .Q(SLF), .preset(1'b0), .en(1'b1), .reset(RESET));  // open: Qn
  J_K_Flip_Flop j_k_ff_2 (.J(ELT), .clk(CLK), .K(ELT), .Q(ELF), .preset(1'b0), .en(1'b1), .reset(RESET));  // open: Qn
  J_K_Flip_Flop j_k_ff_3 (.J(ACT), .clk(CLK), .K(ACT), .Q(ACF), .preset(1'b0), .en(1'b1), .reset(RESET));  // open: Qn
  nor nor_1 (nor_1_out, RFS, RF);
  nor nor_2 (RF, nor_1_out, and_1_out);
  not not_2 (not_2_out, and_2_out);
  and and_3 (and_3_out, BZL, CLK);
  or or_1 (or_1_out, RESET, and_3_out);
  and and_4 (and_4_out, or_1_out, and_2_out);
  or or_2 (or_2_out, RESET, and_5_out);
  and and_5 (and_5_out, not_2_out, or_1_out);
  nor nor_3 (BZF, or_2_out, nor_4_out);
  nor nor_4 (nor_4_out, BZF, and_4_out);
endmodule

module reset (
  input  RESET,
  input  CLK,
  output out_3
);

  wire not_1_out, shift_register_1_out;

  Shift_Register #(.length(1)) shift_register_1 (
    .shift(1'b1), .in(RESET), .clk(CLK), .out(shift_register_1_out), .clr(out_3));  // open: load, d0, q0
  not not_1 (not_1_out, CLK);
  Shift_Register #(.length(1)) shift_register_2 (
    .shift(1'b1), .in(shift_register_1_out), .clk(not_1_out), .out(out_3), .clr(out_3));  // open: load, d0, q0
endmodule
