// Digital circuit sim.dig as structural Verilog
module sim (
  input  clk,
  input  [11:0] INPUT,
  output [11:0] OUT_DATA,
  output OUT_EN,
  output [2:0] INSTR_VAL,
  output [11:0] INSTR_ADDR,
  output [11:0] RESULT
);

  wire ALU_UP, BUSMULT_S0, BUSMULT_S1, button_1_out, CLK_t, IO_S0, LAR_UP, MAR_UP, nALU_CO, nALU_LO,
       nBUSMULT_OE, nLAR_LO, nMAR_CO, not_2_out, not_3_out, nPC_CO, nPC_LO, nRAM_OE, nRST, PC_UP, RAM_WE,
       RAMMULT_S0, RST, u_zero_checker_o;
  wire [11:0] multiplexer_1_out, multiplexer_2_out, notconnected_1_out, notconnected_2_out, pulldown_1_out,
       u_reg_2_o, u_reg_4_o, u_reg_o;

  DipSwitch dipswitch_1 (.out(RST));
  not not_1 (nRST, RST);
  Button button_1 (.out(button_1_out));
  // SwitchDT switchdt_1: pin names not known; wires that end beside it: button_1_out, clk, CLK_t
  not not_2 (not_2_out, LAR_UP);
  PullDown #(.Bits(12)) pulldown_1 (.out(pulldown_1_out));
  \reg  #(.applicationType("GHDL"), .CodeFile("/shared/Documents/Programmation/Electronique/BFComputer/simulation/VHDL/reg.vhdl")) u_reg (
    .CLK(CLK_t), .LO(nRST), .UP(MAR_UP), .CO(nMAR_CO), .i({12{1'b0}}), .o(u_reg_o));
  \reg  #(.applicationType("GHDL"), .CodeFile("/shared/Documents/Programmation/Electronique/BFComputer/simulation/VHDL/reg.vhdl")) u_reg_2 (
    .CLK(CLK_t), .LO(nLAR_LO), .UP(LAR_UP), .CO(not_2_out), .i(INSTR_ADDR), .o(u_reg_2_o));
  \reg  #(.applicationType("GHDL"), .CodeFile("/shared/Documents/Programmation/Electronique/BFComputer/simulation/VHDL/reg.vhdl")) u_reg_3 (
    .CLK(CLK_t), .LO(nPC_LO), .UP(PC_UP), .CO(nPC_CO), .i(pulldown_1_out), .o(INSTR_ADDR));
  zero_checker #(.applicationType("GHDL"), .CodeFile("/shared/Documents/Programmation/Electronique/BFComputer/simulation/VHDL/zero_checker.vhdl")) u_zero_checker (
    .i(pulldown_1_out), .o(u_zero_checker_o));
  EEPROM #(.AddrBits(12), .isProgramMemory("true"), .Bits(3)) PRG_ROM (
    .A(INSTR_ADDR), .CS(1'b1), .WE(1'b0), .OE(1'b1), .D(INSTR_VAL));
  control_logic #(.applicationType("GHDL"), .CodeFile("/shared/Documents/Programmation/Electronique/BFComputer/simulation/VHDL/control_logic.vhdl")) u_control_logic (
    .clk(CLK_t), .rst(RST), .instr(INSTR_VAL), .bus_zc(u_zero_checker_o), .lar_up(LAR_UP), .mar_up(MAR_UP),
    .pc_up(PC_UP), .alu_up(ALU_UP), .ram_we(RAM_WE), .rammult_s0(RAMMULT_S0), .busmult_s0(BUSMULT_S0),
    .busmult_s1(BUSMULT_S1), .io_s0(IO_S0), .io_out(OUT_EN), .lar_lo(nLAR_LO), .mar_co(nMAR_CO),
    .pc_lo(nPC_LO), .pc_co(nPC_CO), .alu_lo(nALU_LO), .alu_co(nALU_CO), .ram_oe(nRAM_OE),
    .busmult_oe(nBUSMULT_OE));
  assign pulldown_1_out = ~nBUSMULT_OE ? multiplexer_1_out : 12'bz;  // DriverInvSel driverinvsel_1
  Multiplexer #(.Selector_Bits(2), .Bits(12)) multiplexer_1 (
    .sel({BUSMULT_S1, BUSMULT_S0}), .in_0(INPUT), .in_1(INSTR_ADDR), .in_2(u_reg_4_o),
    .in_3(notconnected_1_out), .out(multiplexer_1_out));
  not not_3 (not_3_out, nRAM_OE);
  // NotConnected on notconnected_1_out
  Multiplexer #(.Bits(12)) multiplexer_2 (.sel(RAMMULT_S0), .in_0(u_reg_o), .in_1(u_reg_2_o), .out(multiplexer_2_out));
  RAMSinglePort #(.AddrBits(13), .isProgramMemory("true"), .Bits(12)) ramsingleport_1 (
    .A({RAMMULT_S0, multiplexer_2_out}), .str(RAM_WE), .C(CLK_t), .ld(not_3_out), .D(pulldown_1_out));
  Multiplexer #(.Bits(12)) multiplexer_3 (.sel(IO_S0), .in_0(u_reg_4_o), .in_1(pulldown_1_out), .out(OUT_DATA));
  \reg  #(.applicationType("GHDL"), .CodeFile("/shared/Documents/Programmation/Electronique/BFComputer/simulation/VHDL/reg.vhdl")) u_reg_4 (
    .CLK(CLK_t), .LO(nALU_LO), .UP(ALU_UP), .CO(nALU_CO), .i(pulldown_1_out), .o(u_reg_4_o));
  Register #(.Bits(12)) register_1 (.D(OUT_DATA), .C(CLK_t), .en(OUT_EN), .Q(RESULT));
  PullDown #(.Bits(12)) pulldown_2 (.out(RESULT));
  // NotConnected on notconnected_2_out
  LED led_1 (.in(notconnected_2_out[0]));
  LED led_2 (.in(notconnected_2_out[1]));
  LED led_3 (.in(notconnected_2_out[2]));
  LED led_4 (.in(notconnected_2_out[3]));
  LED led_5 (.in(notconnected_2_out[4]));
  LED led_6 (.in(notconnected_2_out[5]));
  LED led_7 (.in(notconnected_2_out[6]));
  LED led_8 (.in(notconnected_2_out[7]));
  LED led_9 (.in(notconnected_2_out[8]));
  LED led_10 (.in(notconnected_2_out[9]));
  LED led_11 (.in(notconnected_2_out[10]));
  LED led_12 (.in(notconnected_2_out[11]));

  // Other names for the same wires on the sheet: IO_OUT = OUT_EN

  // Notes on the sheet:
  //   clk: Hz: 500
  //   MAR
  //   LAR
  //   PC
  //   contents of PRG_ROM (hex, n*v repeats v):
  //   0,4,1,7,4,2,7,4,7,5,0,4,1,7,4,2,7,4,7,5,3,3,4,1,2,0,3,5,2,6,4
  //   ,1,5,5,0,5,5,0,5,0,4,5
  //   IO
  //   ALU
endmodule
